# Fritzing sketch 7seg_kanteidan (saved by Fritzing 0.9.4)
perfboards: 1

parts:
  パーツ1 = Arduino Uno (Rev3)
  R1 = Resistor [tolerance=±5% resistance=100 package=THT]
  R2 = Resistor [tolerance=±5% resistance=100 package=THT]
  R4 = Resistor [tolerance=±5% resistance=100 package=THT]
  R5 = Resistor [tolerance=±5% resistance=100 package=THT]
  R6 = Resistor [tolerance=±5% resistance=100 package=THT]
  R7 = Resistor [tolerance=±5% resistance=100 package=THT]
  R8 = Resistor [tolerance=±5% resistance=100 package=THT]
  J1 = shrouded pin header, 18 pins [form="♂ (shrouded male)"]

nets:
  N1: パーツ1.D8, R1.Pin_1
  N2: パーツ1.D9_PWM, R2.Pin_1
  N3: パーツ1.D10_PWM/SS, R4.Pin_1
  N4: パーツ1.D11_PWM/MOSI, R5.Pin_1
  N5: パーツ1.D12/MISO, R6.Pin_1
  N6: パーツ1.D2, J1.pin1
  N7: パーツ1.D3_PWM, J1.pin2
  N8: パーツ1.D6_PWM, R8.Pin_1
  N9: パーツ1.D7, R7.Pin_1
  N10: R2.Pin_0, J1.pin9

notes:
  7セグLEDのピンは20Pだが19, 20は使わないため18Pのソケットを利用
  ソケットのピン配置は左上が1、右下が18
